# Fritzing sketch Visual Metronome (saved by Fritzing 0.9.3b)

parts:
  Part1 = Arduino Uno (Rev3)
  Part2 = 12 NeoPixel Ring [part_number=1643]

nets:
  N1: Part1.D6_PWM, Part2.IN
  5V: Part1.5V, Part2.VDD
  GND: Part1.GND, Part2.GND

custom parts:
  12 NeoPixel Ring: 12 ultra bright smart LED NeoPixels are arranged in a circle with 1.5" (37mm) outer diameter. The rings are 'chainable' - connect the output pin of one to the input pin of another. Use only one microcontroller pin to control as many as you can chain together! Each LED is addressable as the driver chip is inside the LED. Each one has ~18mA constant current drive so the color will be very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
